// Logisim project PCLtrabCOMP.circ as structural Verilog: 3 circuits, main circuit main
module main (
  input  in_1,
  output [7:0] IRAM,
  output [7:0] out_3,
  output [7:0] out_4,
  output [7:0] out_5,
  output [7:0] out_6,
  output [7:0] out_7,
  output [7:0] out_8,
  output out_9,
  output out_10,
  output out_11,
  output out_12,
  output out_13,
  output out_14,
  output out_15,
  output out_16,
  output out_17,
  output out_18,
  output out_19,
  output out_20,
  output out_21,
  output out_22,
  output [7:0] out_23,
  output [7:0] out_24,
  output [7:0] out_25,
  output out_26,
  output out_27,
  output out_28,
  output out_29,
  output out_30,
  output out_31,
  output out_32,
  output out_33
);

  wire CLK, clock_1_out, comparator_16_eq, comparator_17_lt, comparator_18_gt, comparator_19_eq,
       comparator_19_lt, comparator_20_eq, comparator_20_gt, decoder_3_out0, decoder_3_out1, decoder_3_out2,
       decoder_3_out3, not_1_out, or_1_out, Ra_EQ_0x1, xor_1_out, xor_2_out;
  wire [1:0] Rx, Ry;
  wire [3:0] INSTRUCAO;
  wire [4:0] bit_extender_1_out, bit_extender_2_out, CONTADOR, controlled_buffer_2_out, multiplexer_1_out;
  wire [7:0] adder_1_out, bit_extender_3_out, bit_extender_4_out, bit_extender_5_out, bit_extender_6_out,
       bit_extender_7_out, ENDERECO, multiplexer_2_out, multiplexer_3_out, multiplier_1_out, saidaRa, SR0,
       SR1, SR2, SR3, SRx, SRy, subtractor_1_out;

  Clock clock_1 (.out(clock_1_out));
  not not_1 (not_1_out, out_22);
  assign CLK = not_1_out ? clock_1_out : 1'bz;  // Controlled_Buffer controlled_buffer_1
  assign controlled_buffer_2_out = Ra_EQ_0x1 ? {out_19, INSTRUCAO} : 5'bz;  // Controlled_Buffer controlled_buffer_2
  Comparator comparator_1 (.a(saidaRa), .b(8'h1), .eq(Ra_EQ_0x1));  // open: gt, lt
  PCcontadordoprograma pccontadordoprograma_1 (
    .in_1(controlled_buffer_2_out), .JMP(out_19), .RDM(out_18), .CLK(CLK), .STR(out_20), .CLEAR(in_1),
    .CONTADOR(CONTADOR));
  DEndereco dendereco_1 (.ENDERECO(ENDERECO), .Ry(Ry), .Rx(Rx), .INSTRUCAO(INSTRUCAO));
  Decoder #(.select(2)) decoder_1 (.out0(out_26), .out1(out_28), .out2(out_30), .out3(out_32), .sel(Rx));  // open: en
  Decoder #(.select(2)) decoder_2 (.out0(out_27), .out1(out_29), .out2(out_31), .out3(out_33), .sel(Ry));  // open: en
  Register #(.trigger("falling")) IR (.D(IRAM), .en(1'b1), .clk(CLK), .Q(ENDERECO), .clr(in_1));
  Comparator #(.width(4)) comparator_2 (.a(INSTRUCAO), .b(4'b0010), .eq(out_9));  // open: gt, lt
  Comparator #(.width(4)) comparator_3 (.a(INSTRUCAO), .b(4'b0011), .eq(out_11));  // open: gt, lt
  Comparator #(.width(4)) comparator_4 (.a(INSTRUCAO), .b(4'b0100), .eq(out_13));  // open: gt, lt
  Comparator #(.width(4)) comparator_5 (.a(INSTRUCAO), .b(4'b0101), .eq(out_15));  // open: gt, lt
  Comparator #(.width(4)) comparator_6 (.a(INSTRUCAO), .b(4'b0110), .eq(out_17));  // open: gt, lt
  Comparator #(.width(4)) comparator_7 (.a(INSTRUCAO), .b(4'b0111), .eq(out_19));  // open: gt, lt
  Comparator #(.width(4)) comparator_8 (.a(INSTRUCAO), .b(4'b1000), .eq(out_21));  // open: gt, lt
  assign bit_extender_1_out = {{3{1'b1}}, Ry};  // Bit_Extender bit_extender_1
  assign bit_extender_2_out = {{3{1'b1}}, Rx};  // Bit_Extender bit_extender_2
  Multiplexer #(.select(2), .width(5)) multiplexer_1 (
    .in0(CONTADOR), .in1(bit_extender_1_out), .in2(bit_extender_2_out), .out(multiplexer_1_out),
    .sel({out_20, out_18}));  // open: in3
  Comparator #(.width(4)) comparator_9 (.a(INSTRUCAO), .b(4'b1001), .eq(out_10));  // open: gt, lt
  Comparator #(.width(4)) comparator_10 (.a(INSTRUCAO), .b(4'b1010), .eq(out_12));  // open: gt, lt
  Comparator #(.width(4)) comparator_11 (.a(INSTRUCAO), .b(4'b1011), .eq(out_14));  // open: gt, lt
  Comparator #(.width(4)) comparator_12 (.a(INSTRUCAO), .b(4'b1100), .eq(out_16));  // open: gt, lt
  Comparator #(.width(4)) comparator_13 (.a(INSTRUCAO), .b(4'b1101), .eq(out_18));  // open: gt, lt
  Comparator #(.width(4)) comparator_14 (.a(INSTRUCAO), .b(4'b1110), .eq(out_20));  // open: gt, lt
  Comparator #(.width(4)) comparator_15 (.a(INSTRUCAO), .b(4'b1111), .eq(out_22));  // open: gt, lt
  RAM #(.addrWidth(5), .trigger("falling")) ram_1 (
    .addr(multiplexer_1_out), .we(out_20), .oe(1'b1), .clk(CLK), .din(out_3), .dout(IRAM));
  Decoder #(.select(2)) decoder_3 (
    .out0(decoder_3_out0), .out1(decoder_3_out1), .out2(decoder_3_out2), .out3(decoder_3_out3), .sel(Rx));  // open: en
  or or_1 (or_1_out, out_9, out_11, out_13, out_15, out_17, out_10, out_12, out_21);
  Comparator comparator_16 (.a(SRx), .b(SRy), .eq(comparator_16_eq));  // open: gt, lt
  Comparator comparator_17 (.a(SRx), .b(SRy), .lt(comparator_17_lt));  // open: gt, eq
  Comparator comparator_18 (.a(SRx), .b(SRy), .gt(comparator_18_gt));  // open: eq, lt
  assign bit_extender_3_out = {{7{1'b0}}, comparator_16_eq};  // Bit_Extender bit_extender_3
  assign bit_extender_4_out = {{7{1'b0}}, comparator_17_lt};  // Bit_Extender bit_extender_4
  assign bit_extender_5_out = {{7{1'b0}}, comparator_18_gt};  // Bit_Extender bit_extender_5
  assign out_4 = out_9 ? bit_extender_3_out : 8'bz;  // Controlled_Buffer controlled_buffer_3
  assign out_4 = out_11 ? bit_extender_4_out : 8'bz;  // Controlled_Buffer controlled_buffer_4
  assign out_4 = out_13 ? bit_extender_5_out : 8'bz;  // Controlled_Buffer controlled_buffer_5
  Register RA (.D(out_4), .en(or_1_out), .clk(CLK), .Q(saidaRa), .clr(in_1));
  Register R0 (.D(multiplexer_3_out), .en(decoder_3_out0), .clk(CLK), .Q(SR0), .clr(in_1));
  Register R1 (.D(multiplexer_3_out), .en(decoder_3_out1), .clk(CLK), .Q(SR1), .clr(in_1));
  Register R2 (.D(multiplexer_3_out), .en(decoder_3_out2), .clk(CLK), .Q(SR2), .clr(in_1));
  Register R3 (.D(multiplexer_3_out), .en(decoder_3_out3), .clk(CLK), .Q(SR3), .clr(in_1));
  Comparator comparator_19 (.a(SRx), .b(SRy), .eq(comparator_19_eq), .lt(comparator_19_lt));  // open: gt
  Comparator comparator_20 (.a(SRx), .b(SRy), .gt(comparator_20_gt), .eq(comparator_20_eq));  // open: lt
  Multiplier multiplier_1 (.a(SRx), .b(SRy), .out(multiplier_1_out));  // open: cin, cout
  xor xor_1 (xor_1_out, comparator_19_eq, comparator_19_lt);
  xor xor_2 (xor_2_out, comparator_20_gt, comparator_20_eq);
  assign bit_extender_6_out = {{7{1'b0}}, xor_1_out};  // Bit_Extender bit_extender_6
  assign bit_extender_7_out = {{7{1'b0}}, xor_2_out};  // Bit_Extender bit_extender_7
  assign out_4 = out_21 ? multiplier_1_out : 8'bz;  // Controlled_Buffer controlled_buffer_6
  Multiplexer #(.select(2), .width(8)) multiplexer_2 (
    .in0(SR0), .in1(SR1), .in2(SR2), .in3(SR3), .out(multiplexer_2_out), .sel(Ry));
  assign out_4 = out_15 ? bit_extender_6_out : 8'bz;  // Controlled_Buffer controlled_buffer_7
  assign out_4 = out_17 ? bit_extender_7_out : 8'bz;  // Controlled_Buffer controlled_buffer_8
  Multiplexer #(.select(3), .width(8)) multiplexer_3 (
    .in0(IRAM), .in1(multiplexer_2_out), .in2(out_4), .in4(IRAM), .out(multiplexer_3_out),
    .sel({out_18, out_16, out_14}));  // open: in3, in5, in6, in7
  assign out_3 = out_20 ? multiplexer_2_out : 8'bz;  // Controlled_Buffer controlled_buffer_9
  Subtractor subtractor_1 (.a(SRx), .b(SRy), .out(subtractor_1_out));  // open: bin, bout
  Adder adder_1 (.a(SRx), .b(SRy), .out(adder_1_out));  // open: cin, cout
  assign out_4 = out_12 ? subtractor_1_out : 8'bz;  // Controlled_Buffer controlled_buffer_10
  assign out_4 = out_10 ? adder_1_out : 8'bz;  // Controlled_Buffer controlled_buffer_11
  Multiplexer #(.select(2), .width(8)) multiplexer_4 (.in0(SR0), .in1(SR1), .in2(SR2), .in3(SR3), .out(SRx), .sel(Rx));
  Multiplexer #(.select(2), .width(8)) multiplexer_5 (.in0(SR0), .in1(SR1), .in2(SR2), .in3(SR3), .out(SRy), .sel(Ry));

  assign out_5 = out_4;
  assign out_6 = out_4;
  assign out_7 = out_4;
  assign out_8 = out_4;
  assign out_23 = out_4;
  assign out_24 = out_4;
  assign out_25 = out_4;

  // Other names for the same wires on the sheet: STR = out_20; MOV1 = out_14; MOV2 = out_16; RDM = out_18;
  //   ADD = out_10; bregOUTPUT[7:0] = out_3; CLEAR = in_1; EQ = out_9; GEQ = out_17; GT = out_13; HLT = out_22;
  //   JMP_ADDRESS[4:0] = {out_19, INSTRUCAO}; JMP = out_19; LEQ = out_15; LT = out_11; MUL = out_21; Ra[7:0] = out_4;
  //   Rx0 = out_26; Rx1 = out_28; Rx2 = out_30; Rx3 = out_32; Ry0 = out_27; Ry1 = out_29; Ry2 = out_31; Ry3 = out_33;
  //   SUB = out_12

  // Notes on the sheet:
  //   PC(Contador do Programa)
  //   Decodificador de Endereço
  //   CPU
  //   Decodificador do Registrador(Rx)
  //   Decodificador do Registrador(Ry)
  //   Registrador de Instrução
  //   Decodificador de Instrução
  //   UC(UNIDADE DE CONTROLE)
  //   MEMÓRIA RAM
  //   Banco de Registradores
  //   IGUAL
  //   MENOR
  //   MAIOR
  //   MULTIPLICAÇÃO
  //   MENOR IGUAL
  //   MAIOR IGUAL
  //   Banco de Registradores
  //   SUBTRAÇÃO
  //   ULA
  //   SOMA
endmodule

module PCcontadordoprograma (
  input  [4:0] in_1,
  input  JMP,
  input  RDM,
  input  CLK,
  input  STR,
  input  CLEAR,
  output [4:0] CONTADOR
);

  wire not_1_out, or_1_out;
  wire [4:0] adder_1_out, multiplexer_1_out;

  or or_1 (or_1_out, RDM, STR);
  not not_1 (not_1_out, or_1_out);
  Multiplexer #(.width(5)) multiplexer_1 (.in0(adder_1_out), .in1(in_1), .out(multiplexer_1_out), .sel(JMP));
  Register #(.trigger("falling"), .width(5)) pc (
    .D(multiplexer_1_out), .en(not_1_out), .Q(CONTADOR), .clk(CLK), .clr(CLEAR));
  Adder #(.width(5)) adder_1 (.a(CONTADOR), .b(5'b00001), .out(adder_1_out));  // open: cin, cout

  // Notes on the sheet:
  //   PC(Contador do Programa)
endmodule

module DEndereco (
  input  [7:0] ENDERECO,
  output [1:0] Ry,
  output [1:0] Rx,
  output [3:0] INSTRUCAO
);


  assign INSTRUCAO = ENDERECO[7:4];
  assign Rx = ENDERECO[3:2];
  assign Ry = ENDERECO[1:0];

  // Notes on the sheet:
  //   Decodificador de Endereço
endmodule
